// Logisim project ALU_BOOTH_Registers-rechecked.circ as structural Verilog: 25 circuits, main circuit 25 ALU
module _25_ALU (
  input  [1:0] Control,
  input  [24:0] A,
  input  [24:0] B,
  output [24:0] Output,
  output [3:0] Overflow_Carry_Zero_Negative
);

  wire zero_check_1_out;
  wire [24:0] and_1_a___b, n25_bit_adder_1_out_4, or_1_a___b;

  AND and_1 (.A(A), .B(B), .A___B(and_1_a___b));
  OR or_1 (.A(B), .B(A), .A___B(or_1_a___b));
  _25_bit_ADDER u_25_bit_adder_1 (
    .in_1(Control[0]), .A(A), .B(B), .out_4(n25_bit_adder_1_out_4),
    .Carry_Out(Overflow_Carry_Zero_Negative[2]), .Overflow(Overflow_Carry_Zero_Negative[3]));
  Multiplexer #(.select(2), .width(25), .enable("false")) multiplexer_1 (
    .in0(and_1_a___b), .in1(or_1_a___b), .in2(n25_bit_adder_1_out_4), .in3(n25_bit_adder_1_out_4),
    .out(Output), .sel(Control));
  Negative_check negative_check_1 (.Input(Output), .Out(Overflow_Carry_Zero_Negative[0]));
  not not_1 (Overflow_Carry_Zero_Negative[1], zero_check_1_out);
  Zero_Check zero_check_1 (.Input(Output), .Out(zero_check_1_out));

  // Notes on the sheet:
  //   2207106
  //   00- Adder
  //   01-Substactor
  //   10-And
  //   11-Or
endmodule

module AND (
  input  [24:0] A,
  input  [24:0] B,
  output [24:0] A___B
);

  assign A___B = A & B;  // AND_Gate _25_bit_AND, 25 bits wide

  // Notes on the sheet:
  //   2207106
endmodule

module OR (
  input  [24:0] A,
  input  [24:0] B,
  output [24:0] A___B
);

  assign A___B = A | B;  // OR_Gate _25_bit_OR, 25 bits wide

  // Notes on the sheet:
  //   2207106
endmodule

module _1_bit_ADDER (
  input  Cin,
  input  A,
  input  B,
  output out_4
);

  wire xor_1_out;

  xor xor_1 (xor_1_out, A, B);
  xor SUM (out_4, Cin, xor_1_out);

  // Notes on the sheet:
  //   2207106
endmodule

// ADDER
module _25_bit_ADDER (
  input  in_1,
  input  [24:0] A,
  input  [24:0] B,
  output [24:0] out_4,
  output Carry_Out,
  output Overflow
);

  wire _1, _2, _3, _4, _5, _6, _7, _8, _9, _10, _11, _12, _13, _14, _15, _16, _17, _18, _19, _20, _21, _22,
       _23, _24, aa, and_1_out, and_2_out, bb, cc, dd, ee, ff, gg, hh, ii, jj, kk, ll, mm, nn, not_1_out,
       not_2_out, not_3_out, oo, pp, qq, rr, ss, tt, uu, vv, ww, xx, yy;
  wire [24:0] bit_extender_1_out;

  assign bit_extender_1_out = {{24{in_1}}, in_1};  // Bit_Extender bit_extender_1
  _25_bit_CLG u_25_bit_clg_1 (
    .Cin(in_1), .A(A), .B(B),
    .Cout({Carry_Out, _24, _23, _22, _21, _20, _19, _18, _17, _16, _15, _14, _13, _12, _11, _10, _9, _8, _7, _6, _5, _4, _3, _2, _1}));
  assign {yy, xx, ww, vv, uu, tt, ss, rr, qq, pp, oo, nn, mm, ll, kk, jj, ii, hh, gg, ff, ee, dd, cc, bb, aa} = bit_extender_1_out ^ B;  // XOR_Gate xor_1, 25 bits wide
  _1_bit_ADDER u_1_bit_adder_1 (.Cin(in_1), .A(A[0]), .B(aa), .out_4(out_4[0]));
  _1_bit_ADDER u_1_bit_adder_2 (.Cin(_1), .A(A[1]), .B(bb), .out_4(out_4[1]));
  _1_bit_ADDER u_1_bit_adder_3 (.Cin(_2), .A(A[2]), .B(cc), .out_4(out_4[2]));
  _1_bit_ADDER u_1_bit_adder_4 (.Cin(_3), .A(A[3]), .B(dd), .out_4(out_4[3]));
  _1_bit_ADDER u_1_bit_adder_5 (.Cin(_4), .A(A[4]), .B(ee), .out_4(out_4[4]));
  _1_bit_ADDER u_1_bit_adder_6 (.Cin(_5), .A(A[5]), .B(ff), .out_4(out_4[5]));
  _1_bit_ADDER u_1_bit_adder_7 (.Cin(_6), .A(A[6]), .B(gg), .out_4(out_4[6]));
  _1_bit_ADDER u_1_bit_adder_8 (.Cin(_7), .A(A[7]), .B(hh), .out_4(out_4[7]));
  _1_bit_ADDER u_1_bit_adder_9 (.Cin(_8), .A(A[8]), .B(ii), .out_4(out_4[8]));
  _1_bit_ADDER u_1_bit_adder_10 (.Cin(_9), .A(A[9]), .B(jj), .out_4(out_4[9]));
  _1_bit_ADDER u_1_bit_adder_11 (.Cin(_10), .A(A[10]), .B(kk), .out_4(out_4[10]));
  _1_bit_ADDER u_1_bit_adder_12 (.Cin(_11), .A(A[11]), .B(ll), .out_4(out_4[11]));
  _1_bit_ADDER u_1_bit_adder_13 (.Cin(_12), .A(A[12]), .B(mm), .out_4(out_4[12]));
  _1_bit_ADDER u_1_bit_adder_14 (.Cin(_13), .A(A[13]), .B(nn), .out_4(out_4[13]));
  _1_bit_ADDER u_1_bit_adder_15 (.Cin(_14), .A(A[14]), .B(oo), .out_4(out_4[14]));
  _1_bit_ADDER u_1_bit_adder_16 (.Cin(_15), .A(A[15]), .B(pp), .out_4(out_4[15]));
  _1_bit_ADDER u_1_bit_adder_17 (.Cin(_16), .A(A[16]), .B(qq), .out_4(out_4[16]));
  _1_bit_ADDER u_1_bit_adder_18 (.Cin(_17), .A(A[17]), .B(rr), .out_4(out_4[17]));
  _1_bit_ADDER u_1_bit_adder_19 (.Cin(_18), .A(A[18]), .B(ss), .out_4(out_4[18]));
  _1_bit_ADDER u_1_bit_adder_20 (.Cin(_19), .A(A[19]), .B(tt), .out_4(out_4[19]));
  _1_bit_ADDER u_1_bit_adder_21 (.Cin(_20), .A(A[20]), .B(uu), .out_4(out_4[20]));
  _1_bit_ADDER u_1_bit_adder_22 (.Cin(_21), .A(A[21]), .B(vv), .out_4(out_4[21]));
  _1_bit_ADDER u_1_bit_adder_23 (.Cin(_22), .A(A[22]), .B(ww), .out_4(out_4[22]));
  _1_bit_ADDER u_1_bit_adder_24 (.Cin(_23), .A(A[23]), .B(xx), .out_4(out_4[23]));
  _1_bit_ADDER u_1_bit_adder_25 (.Cin(_24), .A(A[24]), .B(yy), .out_4(out_4[24]));
  not not_1 (not_1_out, out_4[24]);
  not not_2 (not_2_out, A[24]);
  not not_3 (not_3_out, yy);
  and and_1 (and_1_out, not_1_out, A[24], yy);
  and and_2 (and_2_out, out_4[24], not_2_out, not_3_out);
  or or_1 (Overflow, and_1_out, and_2_out);

  // Other names for the same wires on the sheet: _25 = Carry_Out; a_t = A[0]; b_t = A[1]; c = A[2]; d = A[3];
  //   e = A[4]; f = A[5]; g = A[6]; h = A[7]; i = A[8]; j = A[9]; k = A[10]; l = A[11]; m = A[12]; n = A[13];
  //   o = A[14]; p = A[15]; q = A[16]; r = A[17]; s = A[18]; t = A[19]; u = A[20]; v = A[21]; w = A[22]; x = A[23];
  //   y = A[24]; Cin = in_1

  // Notes on the sheet:
  //   2207106
endmodule

module _4_bit_CLG (
  input  Cin,
  input  [3:0] A,
  input  [3:0] B,
  output C1,
  output C2,
  output C3,
  output C4
);

  wire and_5_out, and_6_out, and_7_out, and_8_out, and_9_out, and_10_out, and_11_out, and_12_out, and_13_out,
       and_14_out, G0, G1, G2, G3, xor_1_out, xor_2_out, xor_3_out, xor_4_out, xor_5_out, xor_6_out,
       xor_7_out, xor_8_out;

  xor xor_1 (xor_1_out, Cin, B[0]);
  xor xor_2 (xor_2_out, Cin, B[1]);
  xor xor_3 (xor_3_out, Cin, B[2]);
  xor xor_4 (xor_4_out, Cin, B[3]);
  xor xor_5 (xor_5_out, A[0], xor_1_out);
  xor xor_6 (xor_6_out, A[1], xor_2_out);
  xor xor_7 (xor_7_out, A[2], xor_3_out);
  xor xor_8 (xor_8_out, A[3], xor_4_out);
  and and_1 (G0, A[0], xor_1_out);
  and and_2 (G1, A[1], xor_2_out);
  and and_3 (G2, A[2], xor_3_out);
  and and_4 (G3, A[3], xor_4_out);
  and and_5 (and_5_out, Cin, xor_5_out);
  and and_6 (and_6_out, G0, xor_6_out);
  and and_7 (and_7_out, Cin, xor_5_out, xor_6_out);
  and and_8 (and_8_out, xor_7_out, G1);
  and and_9 (and_9_out, xor_6_out, xor_7_out, G0);
  and and_10 (and_10_out, xor_5_out, xor_6_out, xor_7_out, Cin);
  and and_11 (and_11_out, xor_8_out, G2);
  and and_12 (and_12_out, xor_8_out, xor_7_out, G1);
  and and_13 (and_13_out, xor_6_out, xor_7_out, xor_8_out, G0);
  and and_14 (and_14_out, xor_5_out, xor_6_out, xor_7_out, xor_8_out, Cin);
  or or_1 (C1, G0, and_5_out);
  or or_2 (C2, G1, and_6_out, and_7_out);
  or or_3 (C3, G2, and_8_out, and_9_out, and_10_out);
  or or_4 (C4, G3, and_11_out, and_12_out, and_13_out, and_14_out);

  // Notes on the sheet:
  //   2207106
endmodule

module _1_BIT_CLG (
  input  Cin,
  input  A,
  input  B,
  output Cout
);

  wire and_1_out, and_2_out, xor_1_out, xor_2_out;

  xor xor_1 (xor_1_out, Cin, B);
  xor xor_2 (xor_2_out, A, xor_1_out);
  and and_1 (and_1_out, xor_1_out, A);
  and and_2 (and_2_out, xor_2_out, A);
  or or_1 (Cout, and_1_out, and_2_out);

  // Notes on the sheet:
  //   2207106
endmodule

module _25_bit_CLG (
  input  Cin,
  input  [24:0] A,
  input  [24:0] B,
  output [24:0] Cout
);

  _4_bit_CLG u_4_bit_clg_1 (.Cin(Cin), .C1(Cout[0]), .C2(Cout[1]), .A(A[3:0]), .C3(Cout[2]), .C4(Cout[3]), .B(B[3:0]));
  _4_bit_CLG u_4_bit_clg_2 (
    .Cin(Cout[3]), .C1(Cout[4]), .C2(Cout[5]), .A(A[7:4]), .C3(Cout[6]), .C4(Cout[7]), .B(B[7:4]));
  _4_bit_CLG u_4_bit_clg_3 (
    .Cin(Cout[7]), .C1(Cout[8]), .C2(Cout[9]), .A(A[11:8]), .C3(Cout[10]), .C4(Cout[11]), .B(B[11:8]));
  _4_bit_CLG u_4_bit_clg_4 (
    .Cin(Cout[11]), .C1(Cout[12]), .C2(Cout[13]), .A(A[15:12]), .C3(Cout[14]), .C4(Cout[15]), .B(B[15:12]));
  _4_bit_CLG u_4_bit_clg_5 (
    .Cin(Cout[15]), .C1(Cout[16]), .C2(Cout[17]), .A(A[19:16]), .C3(Cout[18]), .C4(Cout[19]), .B(B[19:16]));
  _4_bit_CLG u_4_bit_clg_6 (
    .Cin(Cout[19]), .C1(Cout[20]), .C2(Cout[21]), .A(A[23:20]), .C3(Cout[22]), .C4(Cout[23]), .B(B[23:20]));
  _1_BIT_CLG u_1_bit_clg_1 (.Cin(Cout[23]), .A(A[24]), .Cout(Cout[24]), .B(B[24]));

  // Notes on the sheet:
  //   2207106
endmodule

// Neg
module Negative_check (
  input  [24:0] Input,
  output Out
);


  assign Out = Input[24];

  // Notes on the sheet:
  //   2207106
endmodule

// Zero
module Zero_Check (
  input  [24:0] Input,
  output Out
);

  or or_1 (Out, Input[0], Input[1], Input[2], Input[3], Input[4], Input[5], Input[6], Input[7], Input[8], Input[9], Input[10], Input[11], Input[12], Input[13], Input[14], Input[15], Input[16], Input[17], Input[18], Input[19], Input[20], Input[21], Input[22], Input[23], Input[24]);

  // Notes on the sheet:
  //   2207106
endmodule

module Counter (
  input  [1:0] Q,
  input  [2:0] T,
  input  C,
  output DA,
  output DB,
  output DC
);

  wire and_1_out, and_2_out, and_3_out, and_4_out, and_5_out, or_4_out, or_5_out, Q0, Q1, Q2, Q3, T0, T1, T2,
       T3, T4, T5, T6, T7;

  Decoder #(.select(2), .enable("false")) decoder_1 (.out0(Q0), .out1(Q1), .out2(Q2), .out3(Q3), .sel(Q));
  Decoder #(.select(3), .enable("false")) decoder_2 (
    .out0(T0), .out1(T1), .out2(T2), .out3(T3), .out4(T4), .out5(T5), .out6(T6), .out7(T7), .sel(T));
  or or_1 (DA, T0, and_5_out, T3, T4, and_1_out, T7);
  or or_2 (DB, T1, and_2_out, T5, T6, T6, T7);
  or or_3 (DC, T5, and_3_out, T3, T4, and_4_out, T7);
  and and_1 (and_1_out, T6, C);
  and and_2 (and_2_out, T2, Q2);
  and and_3 (and_3_out, T2, or_5_out);
  and and_4 (and_4_out, T6, C);
  and and_5 (and_5_out, T2, or_4_out);
  or or_4 (or_4_out, Q0, Q2, Q3);
  or or_5 (or_5_out, Q0, Q1, Q3);

  // Notes on the sheet:
  //   2207106
endmodule

module Sequence_Decoder (
  input  Clk,
  input  Reset,
  input  Q0,
  input  Q_1,
  input  [4:0] Count,
  output Clear_A__Q_1,
  output Load_M__Q__Count,
  output Load_A,
  output C0,
  output C1,
  output Shift_Signal,
  output Decrement_1
);

  wire counter_1_da, counter_1_db, counter_1_dc, decoder_1_out4, nor_1_out;
  wire [2:0] d_ff_1_q;

  nor nor_1 (nor_1_out, Count[2], Count[3], Count[0], Count[1], Count[4]);
  Counter counter_1 (
    .Q({Q0, Q_1}), .T(d_ff_1_q), .C(nor_1_out), .DA(counter_1_da), .DB(counter_1_db), .DC(counter_1_dc));
  Decoder #(.select(3), .enable("false")) decoder_1 (
    .out1(Clear_A__Q_1), .out3(C0), .out4(decoder_1_out4), .out5(Decrement_1), .sel(d_ff_1_q));  // open: out0, out2, out6, out7
  D_Flip_Flop d_ff_1 (.clk(Clk), .D(counter_1_da), .Q(d_ff_1_q[0]), .reset(Reset));  // open: Qn, preset, en
  D_Flip_Flop d_ff_2 (.clk(Clk), .D(counter_1_db), .Q(d_ff_1_q[1]), .reset(Reset));  // open: Qn, preset, en
  D_Flip_Flop d_ff_3 (.clk(Clk), .D(counter_1_dc), .Q(d_ff_1_q[2]), .reset(Reset));  // open: Qn, preset, en
  or or_1 (C1, C0, decoder_1_out4);

  assign Load_A = C1;
  assign Load_M__Q__Count = Clear_A__Q_1;
  assign Shift_Signal = Decrement_1;

  // Notes on the sheet:
  //   2207106
endmodule

module _2_s_comp (
  input  [24:0] A,
  output [24:0] out_2
);

  wire [23:0] not_1_out;
  wire [24:0] adder_1_out;

  not not_1 (not_1_out[0], A[0]);
  not not_2 (not_1_out[1], A[1]);
  not not_3 (not_1_out[2], A[2]);
  not not_4 (not_1_out[3], A[3]);
  not not_5 (not_1_out[4], A[4]);
  not not_6 (not_1_out[5], A[5]);
  not not_7 (not_1_out[6], A[6]);
  not not_8 (not_1_out[7], A[7]);
  not not_9 (not_1_out[8], A[8]);
  not not_10 (not_1_out[9], A[9]);
  not not_11 (not_1_out[10], A[10]);
  not not_12 (not_1_out[11], A[11]);
  not not_13 (not_1_out[12], A[12]);
  not not_14 (not_1_out[13], A[13]);
  not not_15 (not_1_out[14], A[14]);
  not not_16 (not_1_out[15], A[15]);
  not not_17 (not_1_out[16], A[16]);
  not not_18 (not_1_out[17], A[17]);
  not not_19 (not_1_out[18], A[18]);
  not not_20 (not_1_out[19], A[19]);
  not not_21 (not_1_out[20], A[20]);
  not not_22 (not_1_out[21], A[21]);
  not not_23 (not_1_out[22], A[22]);
  not not_24 (not_1_out[23], A[23]);
  Adder #(.width(25)) adder_1 (.a({A[24], not_1_out}), .b(25'h1), .out(adder_1_out));  // open: cin, cout
  Multiplexer #(.width(25), .enable("false")) multiplexer_1 (.in0(A), .in1(adder_1_out), .out(out_2), .sel(A[24]));

  // Notes on the sheet:
  //   2207106
endmodule

module Booth_Algo (
  input  [24:0] Q,
  input  [24:0] M,
  input  Reset,
  output [24:0] out_4,
  output [24:0] out_5
);

  wire clock_1_out, or_1_out, sequence_decoder_1_clear_a__q_1, sequence_decoder_1_decrement_1,
       sequence_decoder_1_load_a, sequence_decoder_1_load_m__q__count, sequence_decoder_1_shift_signal,
       shift_register_2_out, shift_register_3_out, shift_register_4_q0;
  wire [1:0] sequence_decoder_1_c0;
  wire [4:0] counter_1_q;
  wire [24:0] n2_s_comp_1_out_2, n2_s_comp_2_out_2, n25_alu_1_output, shift_register_1_q24;

  Clock clock_1 (.out(clock_1_out));
  Sequence_Decoder sequence_decoder_1 (
    .Clk(clock_1_out), .Reset(Reset), .Q0(out_5[0]), .Q_1(shift_register_4_q0), .Count(counter_1_q),
    .Clear_A__Q_1(sequence_decoder_1_clear_a__q_1), .Load_M__Q__Count(sequence_decoder_1_load_m__q__count),
    .Load_A(sequence_decoder_1_load_a), .C0(sequence_decoder_1_c0[0]), .C1(sequence_decoder_1_c0[1]),
    .Shift_Signal(sequence_decoder_1_shift_signal), .Decrement_1(sequence_decoder_1_decrement_1));
  _2_s_comp u_2_s_comp_1 (.A(Q), .out_2(n2_s_comp_1_out_2));
  Counter_part #(.width(5), .max('h19)) counter_1 (
    .load(or_1_out), .D({5{1'b1}}), .count(sequence_decoder_1_decrement_1), .Q(counter_1_q), .clk(clock_1_out));  // open: carry, clr
  _25_ALU u_25_alu_1 (
    .Control(sequence_decoder_1_c0), .A(out_4), .B(shift_register_1_q24), .Output(n25_alu_1_output));  // open: Overflow_Carry_Zero_Negative
  or or_1 (or_1_out, sequence_decoder_1_decrement_1, sequence_decoder_1_load_m__q__count);
  _2_s_comp u_2_s_comp_2 (.A(M), .out_2(n2_s_comp_2_out_2));
  Shift_Register #(.length(25)) shift_register_1 (
    .shift(1'b0), .clk(clock_1_out), .load(sequence_decoder_1_load_m__q__count), .d0(n2_s_comp_2_out_2[24]),
    .q0(shift_register_1_q24[24]), .d1(n2_s_comp_2_out_2[23]), .q1(shift_register_1_q24[23]),
    .d2(n2_s_comp_2_out_2[22]), .q2(shift_register_1_q24[22]), .d3(n2_s_comp_2_out_2[21]),
    .q3(shift_register_1_q24[21]), .d4(n2_s_comp_2_out_2[20]), .q4(shift_register_1_q24[20]),
    .d5(n2_s_comp_2_out_2[19]), .q5(shift_register_1_q24[19]), .d6(n2_s_comp_2_out_2[18]),
    .q6(shift_register_1_q24[18]), .d7(n2_s_comp_2_out_2[17]), .q7(shift_register_1_q24[17]),
    .d8(n2_s_comp_2_out_2[16]), .q8(shift_register_1_q24[16]), .d9(n2_s_comp_2_out_2[15]),
    .q9(shift_register_1_q24[15]), .d10(n2_s_comp_2_out_2[14]), .q10(shift_register_1_q24[14]),
    .d11(n2_s_comp_2_out_2[13]), .q11(shift_register_1_q24[13]), .d12(n2_s_comp_2_out_2[12]),
    .q12(shift_register_1_q24[12]), .d13(n2_s_comp_2_out_2[11]), .q13(shift_register_1_q24[11]),
    .d14(n2_s_comp_2_out_2[10]), .q14(shift_register_1_q24[10]), .d15(n2_s_comp_2_out_2[9]),
    .q15(shift_register_1_q24[9]), .d16(n2_s_comp_2_out_2[8]), .q16(shift_register_1_q24[8]),
    .d17(n2_s_comp_2_out_2[7]), .q17(shift_register_1_q24[7]), .d18(n2_s_comp_2_out_2[6]),
    .q18(shift_register_1_q24[6]), .d19(n2_s_comp_2_out_2[5]), .q19(shift_register_1_q24[5]),
    .d20(n2_s_comp_2_out_2[4]), .q20(shift_register_1_q24[4]), .d21(n2_s_comp_2_out_2[3]),
    .q21(shift_register_1_q24[3]), .d22(n2_s_comp_2_out_2[2]), .q22(shift_register_1_q24[2]),
    .d23(n2_s_comp_2_out_2[1]), .q23(shift_register_1_q24[1]), .d24(n2_s_comp_2_out_2[0]),
    .q24(shift_register_1_q24[0]));  // open: in, out, clr
  Shift_Register #(.length(25)) shift_register_2 (
    .shift(sequence_decoder_1_shift_signal), .in(out_4[24]), .clk(clock_1_out), .out(shift_register_2_out),
    .load(sequence_decoder_1_load_a), .clr(sequence_decoder_1_clear_a__q_1), .d0(n25_alu_1_output[24]),
    .q0(out_4[24]), .d1(n25_alu_1_output[23]), .q1(out_4[23]), .d2(n25_alu_1_output[22]), .q2(out_4[22]),
    .d3(n25_alu_1_output[21]), .q3(out_4[21]), .d4(n25_alu_1_output[20]), .q4(out_4[20]),
    .d5(n25_alu_1_output[19]), .q5(out_4[19]), .d6(n25_alu_1_output[18]), .q6(out_4[18]),
    .d7(n25_alu_1_output[17]), .q7(out_4[17]), .d8(n25_alu_1_output[16]), .q8(out_4[16]),
    .d9(n25_alu_1_output[15]), .q9(out_4[15]), .d10(n25_alu_1_output[14]), .q10(out_4[14]),
    .d11(n25_alu_1_output[13]), .q11(out_4[13]), .d12(n25_alu_1_output[12]), .q12(out_4[12]),
    .d13(n25_alu_1_output[11]), .q13(out_4[11]), .d14(n25_alu_1_output[10]), .q14(out_4[10]),
    .d15(n25_alu_1_output[9]), .q15(out_4[9]), .d16(n25_alu_1_output[8]), .q16(out_4[8]),
    .d17(n25_alu_1_output[7]), .q17(out_4[7]), .d18(n25_alu_1_output[6]), .q18(out_4[6]),
    .d19(n25_alu_1_output[5]), .q19(out_4[5]), .d20(n25_alu_1_output[4]), .q20(out_4[4]),
    .d21(n25_alu_1_output[3]), .q21(out_4[3]), .d22(n25_alu_1_output[2]), .q22(out_4[2]),
    .d23(n25_alu_1_output[1]), .q23(out_4[1]), .d24(n25_alu_1_output[0]), .q24(out_4[0]));
  Shift_Register #(.length(25)) shift_register_3 (
    .shift(sequence_decoder_1_shift_signal), .in(shift_register_2_out), .clk(clock_1_out),
    .out(shift_register_3_out), .load(sequence_decoder_1_load_m__q__count), .d0(n2_s_comp_1_out_2[24]),
    .q0(out_5[24]), .d1(n2_s_comp_1_out_2[23]), .q1(out_5[23]), .d2(n2_s_comp_1_out_2[22]), .q2(out_5[22]),
    .d3(n2_s_comp_1_out_2[21]), .q3(out_5[21]), .d4(n2_s_comp_1_out_2[20]), .q4(out_5[20]),
    .d5(n2_s_comp_1_out_2[19]), .q5(out_5[19]), .d6(n2_s_comp_1_out_2[18]), .q6(out_5[18]),
    .d7(n2_s_comp_1_out_2[17]), .q7(out_5[17]), .d8(n2_s_comp_1_out_2[16]), .q8(out_5[16]),
    .d9(n2_s_comp_1_out_2[15]), .q9(out_5[15]), .d10(n2_s_comp_1_out_2[14]), .q10(out_5[14]),
    .d11(n2_s_comp_1_out_2[13]), .q11(out_5[13]), .d12(n2_s_comp_1_out_2[12]), .q12(out_5[12]),
    .d13(n2_s_comp_1_out_2[11]), .q13(out_5[11]), .d14(n2_s_comp_1_out_2[10]), .q14(out_5[10]),
    .d15(n2_s_comp_1_out_2[9]), .q15(out_5[9]), .d16(n2_s_comp_1_out_2[8]), .q16(out_5[8]),
    .d17(n2_s_comp_1_out_2[7]), .q17(out_5[7]), .d18(n2_s_comp_1_out_2[6]), .q18(out_5[6]),
    .d19(n2_s_comp_1_out_2[5]), .q19(out_5[5]), .d20(n2_s_comp_1_out_2[4]), .q20(out_5[4]),
    .d21(n2_s_comp_1_out_2[3]), .q21(out_5[3]), .d22(n2_s_comp_1_out_2[2]), .q22(out_5[2]),
    .d23(n2_s_comp_1_out_2[1]), .q23(out_5[1]), .d24(n2_s_comp_1_out_2[0]), .q24(out_5[0]));  // open: clr
  Shift_Register #(.length(1)) shift_register_4 (
    .shift(sequence_decoder_1_shift_signal), .in(shift_register_3_out), .clk(clock_1_out),
    .clr(sequence_decoder_1_clear_a__q_1), .q0(shift_register_4_q0));  // open: out, load, d0

  // Notes on the sheet:
  //   2207106
endmodule

module _4_bit_PLR (
  input  load,
  input  clock,
  input  [3:0] \input ,
  input  clear,
  output [3:0] \output 
);

  wire and_1_out, and_2_out, and_3_out, and_4_out, and_5_out, and_6_out, and_7_out, and_8_out, not_1_out,
       not_2_out, not_3_out, not_4_out;

  not not_1 (not_1_out, \input [0]);
  not not_2 (not_2_out, \input [1]);
  not not_3 (not_3_out, \input [2]);
  not not_4 (not_4_out, \input [3]);
  and and_1 (and_1_out, \input [0], load);
  and and_2 (and_2_out, not_1_out, load);
  and and_3 (and_3_out, \input [1], load);
  and and_4 (and_4_out, not_2_out, load);
  and and_5 (and_5_out, \input [2], load);
  and and_6 (and_6_out, not_3_out, load);
  and and_7 (and_7_out, \input [3], load);
  and and_8 (and_8_out, not_4_out, load);
  J_K_Flip_Flop j_k_ff_1 (
    .J(and_1_out), .clk(clock), .K(and_2_out), .Q(\output [0]), .reset(clear));  // open: Qn, preset, en
  J_K_Flip_Flop j_k_ff_2 (
    .J(and_3_out), .clk(clock), .K(and_4_out), .Q(\output [1]), .reset(clear));  // open: Qn, preset, en
  J_K_Flip_Flop j_k_ff_3 (
    .J(and_5_out), .clk(clock), .K(and_6_out), .Q(\output [2]), .reset(clear));  // open: Qn, preset, en
  J_K_Flip_Flop j_k_ff_4 (
    .J(and_7_out), .clk(clock), .K(and_8_out), .Q(\output [3]), .reset(clear));  // open: Qn, preset, en

  // Notes on the sheet:
  //   2207106
endmodule

module _2_bit_PLR (
  input  load,
  input  clock,
  input  clear,
  input  [1:0] \input ,
  output [1:0] \output 
);

  _1_bit_PLR u_1_bit_plr_1 (.\output (\output [0]), .\input (\input [0]), .load(load), .clr(clear), .clock(clock));
  _1_bit_PLR u_1_bit_plr_2 (.\output (\output [1]), .\input (\input [1]), .load(load), .clr(clear), .clock(clock));

  // Notes on the sheet:
  //   2207106
endmodule

module _1_bit_PLR (
  input  load,
  input  clock,
  input  \input ,
  input  clr,
  output \output 
);

  wire and_1_out, and_2_out, not_1_out;

  not not_1 (not_1_out, \input );
  and and_1 (and_1_out, not_1_out, load);
  and and_2 (and_2_out, \input , load);
  J_K_Flip_Flop j_k_ff_1 (
    .J(and_2_out), .clk(clock), .K(and_1_out), .Q(\output ), .reset(clr));  // open: Qn, preset, en

  // Notes on the sheet:
  //   2207106
endmodule

module ACR_25_bit_PLR (
  input  load,
  input  clock,
  input  clear,
  input  [24:0] \input ,
  output [24:0] \output 
);

  _4_bit_PLR u_4_bit_plr_1 (
    .\output (\output [3:0]), .\input (\input [3:0]), .clear(clear), .load(load), .clock(clock));
  _4_bit_PLR u_4_bit_plr_2 (
    .\output (\output [7:4]), .\input (\input [7:4]), .clear(clear), .load(load), .clock(clock));
  _4_bit_PLR u_4_bit_plr_3 (
    .\output (\output [11:8]), .\input (\input [11:8]), .clear(clear), .load(load), .clock(clock));
  _4_bit_PLR u_4_bit_plr_4 (
    .\output (\output [15:12]), .\input (\input [15:12]), .clear(clear), .load(load), .clock(clock));
  _4_bit_PLR u_4_bit_plr_5 (
    .\output (\output [19:16]), .\input (\input [19:16]), .clear(clear), .load(load), .clock(clock));
  _4_bit_PLR u_4_bit_plr_6 (
    .\output (\output [23:20]), .\input (\input [23:20]), .clear(clear), .load(load), .clock(clock));
  _1_bit_PLR u_1_bit_plr_1 (.\output (\output [24]), .\input (\input [24]), .load(load), .clr(clear), .clock(clock));

  // Notes on the sheet:
  //   2207106
endmodule

module _2_bit_cpl (
  input  Cin,
  input  count,
  input  LOAD,
  input  [1:0] in_4,
  input  CLR,
  input  CLK,
  output [1:0] out_7,
  output Cout
);

  wire and_1_out, and_2_out, and_3_out, and_4_out, and_5_out, and_6_out, and_7_out, not_1_out, not_2_out,
       not_3_out, or_1_out, or_2_out, or_3_out, or_4_out;

  and and_1 (and_1_out, count, not_1_out);
  not not_1 (not_1_out, LOAD);
  not not_2 (not_2_out, in_4[0]);
  not not_3 (not_3_out, in_4[1]);
  and and_2 (and_2_out, LOAD, in_4[0]);
  and and_3 (and_3_out, LOAD, not_2_out);
  and and_4 (and_4_out, LOAD, in_4[1]);
  and and_5 (and_5_out, LOAD, not_3_out);
  and and_6 (and_6_out, and_1_out, Cin);
  and and_7 (and_7_out, and_1_out, Cin, out_7[0]);
  or or_1 (or_1_out, and_2_out, and_6_out);
  or or_2 (or_2_out, and_6_out, and_3_out);
  or or_3 (or_3_out, and_4_out, and_7_out);
  or or_4 (or_4_out, and_7_out, and_5_out);
  J_K_Flip_Flop j_k_ff_1 (.J(or_1_out), .clk(CLK), .K(or_2_out), .Q(out_7[0]), .reset(CLR));  // open: Qn, preset, en
  J_K_Flip_Flop j_k_ff_2 (.J(or_3_out), .clk(CLK), .K(or_4_out), .Q(out_7[1]), .reset(CLR));  // open: Qn, preset, en
  and and_8 (Cout, out_7[0], out_7[1], Cin, and_1_out);

  // Notes on the sheet:
  //   2207106
endmodule

module _1_bit_cpl (
  input  Cin,
  input  count,
  input  LOAD,
  input  in_4,
  input  CLR,
  input  CLK,
  output out_7
);

  wire and_1_out, and_2_out, and_3_out, and_4_out, not_1_out, not_2_out, or_1_out, or_2_out;

  and and_1 (and_1_out, count, not_1_out);
  not not_1 (not_1_out, LOAD);
  not not_2 (not_2_out, in_4);
  and and_2 (and_2_out, LOAD, in_4);
  and and_3 (and_3_out, LOAD, not_2_out);
  and and_4 (and_4_out, and_1_out, Cin);
  or or_1 (or_1_out, and_2_out, and_4_out);
  or or_2 (or_2_out, and_4_out, and_3_out);
  J_K_Flip_Flop j_k_ff_1 (.J(or_1_out), .clk(CLK), .K(or_2_out), .Q(out_7), .reset(CLR));  // open: Qn, preset, en

  // Notes on the sheet:
  //   2207106
endmodule

module _4_bit_cpl (
  input  count,
  input  load,
  input  [3:0] \input ,
  input  clock,
  input  reset,
  output [3:0] \output ,
  output Cout
);

  wire n2_bit_cpl_1_cout;

  _2_bit_cpl u_2_bit_cpl_1 (
    .Cin(count), .count(count), .LOAD(load), .in_4(\input [1:0]), .out_7(\output [1:0]), .CLR(reset),
    .CLK(clock), .Cout(n2_bit_cpl_1_cout));
  _2_bit_cpl u_2_bit_cpl_2 (
    .Cin(n2_bit_cpl_1_cout), .count(count), .LOAD(load), .in_4(\input [3:2]), .out_7(\output [3:2]),
    .CLR(reset), .CLK(clock), .Cout(Cout));

  // Notes on the sheet:
  //   2207106
endmodule

module MBR_25_bit_CPL (
  input  load,
  input  count,
  input  clock,
  input  reset,
  input  [24:0] in_5,
  output [24:0] out_6
);

  wire clock_1_out, n4_bit_cpl_1_cout, n4_bit_cpl_2_cout, n4_bit_cpl_3_cout, n4_bit_cpl_4_cout,
       n4_bit_cpl_5_cout, n4_bit_cpl_6_cout;

  Clock clock_1 (.out(clock_1_out));
  _4_bit_cpl u_4_bit_cpl_1 (
    .load(load), .count(count), .\input (in_5[3:0]), .clock(clock_1_out), .reset(reset),
    .\output (out_6[3:0]), .Cout(n4_bit_cpl_1_cout));
  _4_bit_cpl u_4_bit_cpl_2 (
    .load(load), .count(n4_bit_cpl_1_cout), .\input (in_5[7:4]), .clock(clock_1_out), .reset(reset),
    .\output (out_6[7:4]), .Cout(n4_bit_cpl_2_cout));
  _4_bit_cpl u_4_bit_cpl_3 (
    .load(load), .count(n4_bit_cpl_2_cout), .\input (in_5[11:8]), .clock(clock_1_out), .reset(reset),
    .\output (out_6[11:8]), .Cout(n4_bit_cpl_3_cout));
  _4_bit_cpl u_4_bit_cpl_4 (
    .load(load), .count(n4_bit_cpl_3_cout), .\input (in_5[15:12]), .clock(clock_1_out), .reset(reset),
    .\output (out_6[15:12]), .Cout(n4_bit_cpl_4_cout));
  _4_bit_cpl u_4_bit_cpl_5 (
    .load(load), .count(n4_bit_cpl_4_cout), .\input (in_5[19:16]), .clock(clock_1_out), .reset(reset),
    .\output (out_6[19:16]), .Cout(n4_bit_cpl_5_cout));
  _4_bit_cpl u_4_bit_cpl_6 (
    .load(load), .count(n4_bit_cpl_5_cout), .\input (in_5[23:20]), .clock(clock_1_out), .reset(reset),
    .\output (out_6[23:20]), .Cout(n4_bit_cpl_6_cout));
  _1_bit_cpl u_1_bit_cpl_1 (
    .Cin(n4_bit_cpl_6_cout), .count(count), .LOAD(load), .in_4(in_5[24]), .out_7(out_6[24]), .CLR(reset),
    .CLK(clock_1_out));

  // Notes on the sheet:
  //   2207106
endmodule

module Program_Counter (
  input  load,
  input  count,
  input  clock,
  input  reset,
  input  [4:0] in_5,
  output [4:0] out_6
);

  wire n4_bit_cpl_1_cout;

  _4_bit_cpl u_4_bit_cpl_1 (
    .load(load), .count(count), .\input (in_5[3:0]), .clock(clock), .reset(reset), .\output (out_6[3:0]),
    .Cout(n4_bit_cpl_1_cout));
  _1_bit_cpl u_1_bit_cpl_1 (
    .Cin(n4_bit_cpl_1_cout), .count(count), .LOAD(load), .in_4(in_5[4]), .out_7(out_6[4]), .CLR(reset),
    .CLK(clock));

  // Notes on the sheet:
  //   2207106
endmodule

module MAR (
  input  clr,
  input  clock,
  input  load,
  input  [4:0] in_4,
  output [4:0] out_5
);

  _4_bit_PLR u_4_bit_plr_1 (.\output (out_5[3:0]), .\input (in_4[3:0]), .clear(clr), .load(load), .clock(clock));
  _1_bit_PLR u_1_bit_plr_1 (.\output (out_5[4]), .\input (in_4[4]), .load(load), .clr(clr), .clock(clock));

  // Notes on the sheet:
  //   2207106
endmodule

module IR (
  input  load,
  input  [3:0] \input ,
  input  clear,
  output [3:0] \output 
);

  wire and_1_out, and_2_out, and_3_out, and_4_out, and_5_out, and_6_out, and_7_out, and_8_out, clock_1_out,
       not_1_out, not_2_out, not_3_out, not_4_out;

  not not_1 (not_1_out, \input [0]);
  not not_2 (not_2_out, \input [1]);
  not not_3 (not_3_out, \input [2]);
  not not_4 (not_4_out, \input [3]);
  and and_1 (and_1_out, \input [0], load);
  and and_2 (and_2_out, not_1_out, load);
  and and_3 (and_3_out, \input [1], load);
  and and_4 (and_4_out, not_2_out, load);
  and and_5 (and_5_out, \input [2], load);
  and and_6 (and_6_out, not_3_out, load);
  and and_7 (and_7_out, \input [3], load);
  and and_8 (and_8_out, not_4_out, load);
  Clock clock_1 (.out(clock_1_out));
  J_K_Flip_Flop j_k_ff_1 (
    .J(and_1_out), .clk(clock_1_out), .K(and_2_out), .Q(\output [0]), .reset(clear));  // open: Qn, preset, en
  J_K_Flip_Flop j_k_ff_2 (
    .J(and_3_out), .clk(clock_1_out), .K(and_4_out), .Q(\output [1]), .reset(clear));  // open: Qn, preset, en
  J_K_Flip_Flop j_k_ff_3 (
    .J(and_5_out), .clk(clock_1_out), .K(and_6_out), .Q(\output [2]), .reset(clear));  // open: Qn, preset, en
  J_K_Flip_Flop j_k_ff_4 (
    .J(and_7_out), .clk(clock_1_out), .K(and_8_out), .Q(\output [3]), .reset(clear));  // open: Qn, preset, en

  // Notes on the sheet:
  //   2207106
endmodule
