// Logisim project MiniComputer-2207106.circ as structural Verilog: 5 circuits, main circuit main
module main (
  input  in_1,
  output [3:0] out_2,
  output [24:0] out_3,
  output [24:0] out_4
);

  wire ACC_to_B, B_ADD__to_MAR, B_ADD__to_PC, B_OP__to_IR, B_plus_plus, B_to_Memory, BZ, clock, clock_1_out,
       Exe, Fetch, H, Halt, j_k_ff_1_q, Load, MAR_to_PC, Memory_to_B, or_1_out, or_2_out, or_3_out, or_4_out,
       PC_plus_plus, PC_to_B, PC_to_MAR, ShiftL, ShiftR, Store_to_ACC;
  wire [1:0] alu_control_1_out, priority_encoder_1_out, priority_encoder_2_out;
  wire [2:0] undriven, undriven_3, undriven_4, undriven_5;
  wire [3:0] undriven_2;
  wire [4:0] MAR, multiplexer_2_out, multiplexer_3_out, PC;
  wire [24:0] LS, M_OUT, multiplexer_1_out, multiplexer_4_out, RES, RS;

  Clock clock_1 (.out(clock_1_out));
  and and_1 (clock, clock_1_out, H);
  D_Flip_Flop u_H (.clk(clock), .D(Halt), .Q(H), .reset(in_1));  // open: Qn, preset, en
  J_K_Flip_Flop j_k_ff_1 (.J(Exe), .clk(clock), .K(Fetch), .Q(j_k_ff_1_q), .reset(in_1));  // open: Qn, preset, en
  Multiplexer #(.select(2), .width(25)) multiplexer_1 (
    .in0(M_OUT), .in1(out_3), .in2({undriven_5, undriven_4, undriven_3, 4'b1000, undriven_2, undriven, PC}),
    .out(multiplexer_1_out), .sel(priority_encoder_1_out));  // open: in3, en
  Priority_Encoder #(.select(2)) priority_encoder_1 (
    .in0(Memory_to_B), .in1(ACC_to_B), .in2(PC_to_B), .out(priority_encoder_1_out));  // open: in3
  Control_Unit control_unit_1 (
    .BZ(BZ), .clock(clock), .reset(in_1), .F(j_k_ff_1_q), .start(H), .IR(out_2),
    .B_Address_____PC(B_ADD__to_PC), .PC____MAR(PC_to_MAR), .Memory____Buffer(Memory_to_B),
    .Fetch_Starts(Fetch), .PC_plus_plus(PC_plus_plus), .Buffer_OP_____IR(B_OP__to_IR), .Halt(Halt),
    .Load(Load), .Execution_Starts(Exe), .Shift_Right(ShiftR), .B_address_____MAR(B_ADD__to_MAR),
    .Buffer_to_Memory(B_to_Memory), .Shift_Left(ShiftL), .Store_to_Accumulator(Store_to_ACC),
    .PC_to_Buffer(PC_to_B), .Accumulator_to_Buffer(ACC_to_B), .Buffer_Increment(B_plus_plus),
    .MAR_to_PC(MAR_to_PC));
  MBR_25_bit_CPL mbr_25_bit_cpl_1 (
    .load(or_1_out), .count(B_plus_plus), .Clock(clock), .reset(in_1), .in_5(multiplexer_1_out), .out_6(out_4));
  or or_1 (or_1_out, Memory_to_B, ACC_to_B, PC_to_B);
  Zero_Check zero_check_1 (.Input(out_4), .Out(BZ));
  or or_2 (or_2_out, PC_to_MAR, B_ADD__to_MAR);
  IR ir_1 (.load(B_OP__to_IR), .\input (out_4[15:12]), .Clock(clock), .clear(in_1), .\output (out_2));
  Left_Shift left_shift_1 (.in_1(out_3), .out_2(LS));
  ALU_Control alu_control_1 (.IR(out_2), .Out(alu_control_1_out));
  Multiplexer #(.width(5)) multiplexer_2 (
    .in0(out_4[4:0]), .in1(PC), .out(multiplexer_2_out), .sel(PC_to_MAR));  // open: en
  _25_ALU u_25_alu_1 (
    .Control(alu_control_1_out), .A(out_3), .B(out_4), .Output(RES));  // open: Overflow_Carry_Zero_Negative
  MAR mar_1 (.out_5(MAR), .in_4(multiplexer_2_out), .clr(in_1), .clock(clock), .load(or_2_out));
  Right_Shift right_shift_1 (.in_1(out_3), .out_2(RS));
  RAM #(.addrWidth(5), .dataWidth(25), .bus("separate")) ram_1 (
    .addr(MAR), .din(out_4), .data(M_OUT), .str(B_to_Memory), .clk(clock), .ld(Memory_to_B));  // open: sel, clr
  or or_3 (or_3_out, Store_to_ACC, Load, ShiftR, ShiftL);
  Priority_Encoder #(.select(2)) priority_encoder_2 (
    .in0(Store_to_ACC), .in1(Load), .in2(ShiftR), .in3(ShiftL), .out(priority_encoder_2_out));
  Multiplexer #(.width(5)) multiplexer_3 (
    .in0(MAR), .in1(out_4[4:0]), .out(multiplexer_3_out), .sel(B_ADD__to_PC));  // open: en
  or or_4 (or_4_out, B_ADD__to_PC, MAR_to_PC);
  Multiplexer #(.select(2), .width(25)) multiplexer_4 (
    .in0(RES), .in1(out_4), .in2(RS), .in3(LS), .out(multiplexer_4_out), .sel(priority_encoder_2_out));  // open: en
  ACR_25_bit_PLR acr_25_bit_plr_1 (
    .\output (out_3), .\input (multiplexer_4_out), .load(or_3_out), .clock(clock), .clear(in_1));
  Program_Counter program_counter_1 (
    .load(or_4_out), .count(PC_plus_plus), .clock(clock), .reset(in_1), .in_5(multiplexer_3_out), .out_6(PC));

  // Other names for the same wires on the sheet: AC[24:0] = out_3; IR[3:0] = out_2; B_ADD[4:0] = out_4[4:0];
  //   MBR[24:0] = out_4; B_OP[3:0] = out_4[15:12]; reset = in_1

  // Notes on the sheet:
  //   2207106
  //   MBR
  //   2207106
  //   LShift
  //   MAR
  //   ALU
  //   IR
  //   RShift
  //   PC
  //   ACCUMULATOR
  //   0-AND
  //   1-OR
  //   2-ADD
  //   3-SUB
  //   4-load
  //   5-Store
  //   6-ISZ
  //   7-BSB
  //   8-BUN
  //   9-HALT
  //   10-ShiftR
  //   11-ShiftL
endmodule

module Control_Unit (
  input  BZ,
  input  clock,
  input  reset,
  input  F,
  input  start,
  input  [3:0] IR,
  output B_Address_____PC,
  output PC____MAR,
  output Memory____Buffer,
  output Fetch_Starts,
  output PC_plus_plus,
  output Buffer_OP_____IR,
  output Halt,
  output Load,
  output Execution_Starts,
  output Shift_Right,
  output B_address_____MAR,
  output Buffer_to_Memory,
  output Shift_Left,
  output Store_to_Accumulator,
  output PC_to_Buffer,
  output Accumulator_to_Buffer,
  output Buffer_Increment,
  output MAR_to_PC
);

  wire and_7_out, and_8_out, and_9_out, and_10_out, and_11_out, and_15_out, not_1_out, not_2_out, not_3_out,
       not_4_out, or_1_out, or_2_out, or_3_out, or_4_out, q0, q1, q2, q3, q4, q5, q6, q7, q8, q9, q10, q11,
       t0, t1, t2, t3;
  wire [1:0] counter_1_q;

  not not_1 (not_1_out, F);
  not not_2 (not_2_out, F);
  or or_1 (or_1_out, q0, q1, q2, q3, q4, q5, q6, q7);
  or or_2 (or_2_out, q0, q1, q2, q3);
  and and_1 (PC____MAR, not_1_out, t0);
  and and_2 (Buffer_OP_____IR, not_2_out, t2);
  not not_3 (not_3_out, F);
  and and_3 (B_address_____MAR, F, t0);
  and and_4 (Accumulator_to_Buffer, F, q5, t2);
  and and_5 (Execution_Starts, not_3_out, or_1_out, t3);
  and and_6 (Store_to_Accumulator, F, or_2_out, t3);
  Decoder #(.select(4)) decoder_1 (
    .out0(q0), .out1(q1), .out2(q2), .out3(q3), .out4(q4), .out5(q5), .out6(q6), .out7(q7), .out8(q8),
    .out9(q9), .out10(q10), .out11(q11), .sel(IR));  // open: out12, out13, out14, out15, en
  not not_4 (not_4_out, F);
  or or_3 (or_3_out, q0, q1, q2, q3, q4, q5, q6);
  or or_4 (or_4_out, q5, q6);
  and and_7 (and_7_out, not_4_out, t1);
  and and_8 (and_8_out, F, or_3_out, t1);
  and and_9 (and_9_out, F, BZ, q6, t3);
  and and_10 (and_10_out, F, q7, t3);
  and and_11 (and_11_out, F, or_4_out, t3);
  and and_12 (Buffer_Increment, F, q6, t2);
  and and_13 (B_Address_____PC, q8, t3);
  or or_5 (Memory____Buffer, and_7_out, and_8_out);
  or or_6 (PC_plus_plus, and_7_out, and_9_out, and_10_out);
  or or_7 (Buffer_to_Memory, and_10_out, and_11_out);
  Counter #(.width(2), .max('h3)) counter_1 (
    .load(1'b0), .Q(counter_1_q), .clk(clock), .clr(reset));  // open: D, count, carry
  and and_14 (Fetch_Starts, F, t3);
  and and_15 (and_15_out, q9, t3);
  and and_16 (Load, F, q4, t2);
  and and_17 (Shift_Right, q10, t3);
  and and_18 (Shift_Left, q11, t3);
  and and_19 (MAR_to_PC, F, q7, t2);
  Decoder #(.select(2)) decoder_2 (.out0(t0), .out1(t1), .out2(t2), .out3(t3), .sel(counter_1_q));  // open: en
  not not_5 (Halt, and_15_out);

  assign PC_to_Buffer = MAR_to_PC;

  // Notes on the sheet:
  //   2207106
  //   2207106
endmodule

module Right_Shift (
  input  [24:0] in_1,
  output [24:0] out_2
);


  assign out_2 = {1'b0, in_1[24:1]};

  // Notes on the sheet:
  //   2207106
endmodule

module Left_Shift (
  input  [24:0] in_1,
  output [24:0] out_2
);


  assign out_2 = {in_1[23:0], 1'b0};

  // Notes on the sheet:
  //   2207106
endmodule

// ALUC
module ALU_Control (
  input  [3:0] IR,
  output [1:0] Out
);

  wire [1:0] undriven;

  Multiplexer #(.select(4), .width(2)) multiplexer_1 (
    .in0(2'b00), .in1(2'b01), .in2(2'b10), .in3(2'b11), .in4(undriven), .in5(undriven), .in6(undriven),
    .in7(undriven), .in8(undriven), .in9(undriven), .in10(undriven), .in11(undriven), .in12(undriven),
    .in13(undriven), .in14(undriven), .in15(undriven), .out(Out), .sel(IR));  // open: en

  // Notes on the sheet:
  //   2207106
endmodule
