// Logisim project 25 ADDER.circ as structural Verilog: 5 circuits, main circuit main
module main (
  input  [24:0] in_1,
  input  [24:0] in_2,
  output [24:0] out_3,
  output [24:0] out_4
);

  AND and_1 (.Input_25_bit(in_1), .Input_25_bit_2(in_2), .Output_25_bit(out_3));
  OR or_1 (.in_1(in_1), .in_2(in_2), .out_3(out_4));
endmodule

module AND (
  input  [24:0] Input_25_bit,
  input  [24:0] Input_25_bit_2,
  output [24:0] Output_25_bit
);

  assign Output_25_bit = Input_25_bit & Input_25_bit_2;  // AND_Gate _25AND, 25 bits wide
endmodule

module OR (
  input  [24:0] in_1,
  input  [24:0] in_2,
  output [24:0] out_3
);

  assign out_3 = in_1 | in_2;  // OR_Gate _25OR, 25 bits wide
endmodule

module ADDER (
  input  A,
  input  B,
  input  Cin,
  output Sum,
  output Carry
);

  wire and_1_out, and_2_out, xor_1_out;

  xor xor_1 (xor_1_out, A, B);
  xor xor_2 (Sum, xor_1_out, Cin);
  and and_1 (and_1_out, A, B);
  and and_2 (and_2_out, xor_1_out, Cin);
  or or_1 (Carry, and_1_out, and_2_out);
endmodule

module _25_ADDER (
  input  in_1,
  input  in_2,
  input  in_3,
  input  in_4,
  input  in_5,
  input  in_6,
  input  in_7,
  input  in_8,
  input  in_9,
  input  in_10,
  input  in_11,
  input  in_12,
  input  in_13,
  input  in_14,
  input  in_15,
  input  in_16,
  input  in_17,
  input  in_18,
  input  in_19,
  input  in_20,
  input  in_21,
  input  in_22,
  input  in_23,
  input  in_24,
  input  in_25,
  input  Cin,
  input  in_27,
  input  in_28,
  input  in_29,
  input  in_30,
  input  in_31,
  input  in_32,
  input  in_33,
  input  in_34,
  input  in_35,
  input  in_36,
  input  in_37,
  input  in_38,
  input  in_39,
  input  in_40,
  input  in_41,
  input  in_42,
  input  in_43,
  input  in_44,
  input  in_45,
  input  in_46,
  input  in_47,
  input  in_48,
  input  in_49,
  input  in_50,
  input  in_51,
  output out_52,
  output out_53,
  output out_54,
  output out_55,
  output out_56,
  output out_57,
  output out_58,
  output out_59,
  output out_60,
  output out_61,
  output out_62,
  output out_63,
  output out_64,
  output out_65,
  output out_66,
  output out_67,
  output out_68,
  output out_69,
  output out_70,
  output out_71,
  output out_72,
  output out_73,
  output out_74,
  output out_75,
  output out_76,
  output F_carry
);

  wire adder_1_carry, adder_2_carry, adder_3_carry, adder_4_carry, adder_5_carry, adder_6_carry,
       adder_7_carry, adder_8_carry, adder_9_carry, adder_10_carry, adder_11_carry, adder_12_carry,
       adder_13_carry, adder_14_carry, adder_15_carry, adder_16_carry, adder_17_carry, adder_18_carry,
       adder_19_carry, adder_20_carry, adder_21_carry, adder_22_carry, adder_23_carry, adder_24_carry;

  ADDER adder_1 (.A(in_28), .B(in_2), .Cin(adder_2_carry), .Sum(out_53), .Carry(adder_1_carry));
  ADDER adder_2 (.A(in_27), .B(in_1), .Cin(Cin), .Sum(out_52), .Carry(adder_2_carry));
  ADDER adder_3 (.A(in_30), .B(in_4), .Cin(adder_4_carry), .Sum(out_55), .Carry(adder_3_carry));
  ADDER adder_4 (.A(in_29), .B(in_3), .Cin(adder_1_carry), .Sum(out_54), .Carry(adder_4_carry));
  ADDER adder_5 (.A(in_31), .B(in_5), .Cin(adder_3_carry), .Sum(out_56), .Carry(adder_5_carry));
  ADDER adder_6 (.A(in_32), .B(in_6), .Cin(adder_5_carry), .Sum(out_57), .Carry(adder_6_carry));
  ADDER adder_7 (.A(in_34), .B(in_8), .Cin(adder_8_carry), .Sum(out_59), .Carry(adder_7_carry));
  ADDER adder_8 (.A(in_33), .B(in_7), .Cin(adder_6_carry), .Sum(out_58), .Carry(adder_8_carry));
  ADDER adder_9 (.A(in_36), .B(in_10), .Cin(adder_10_carry), .Sum(out_61), .Carry(adder_9_carry));
  ADDER adder_10 (.A(in_35), .B(in_9), .Cin(adder_7_carry), .Sum(out_60), .Carry(adder_10_carry));
  ADDER adder_11 (.A(in_37), .B(in_11), .Cin(adder_9_carry), .Sum(out_62), .Carry(adder_11_carry));
  ADDER adder_12 (.A(in_38), .B(in_12), .Cin(adder_11_carry), .Sum(out_63), .Carry(adder_12_carry));
  ADDER adder_13 (.A(in_39), .B(in_13), .Cin(adder_12_carry), .Sum(out_64), .Carry(adder_13_carry));
  ADDER adder_14 (.A(in_40), .B(in_14), .Cin(adder_13_carry), .Sum(out_65), .Carry(adder_14_carry));
  ADDER adder_15 (.A(in_42), .B(in_16), .Cin(adder_16_carry), .Sum(out_67), .Carry(adder_15_carry));
  ADDER adder_16 (.A(in_41), .B(in_15), .Cin(adder_14_carry), .Sum(out_66), .Carry(adder_16_carry));
  ADDER adder_17 (.A(in_44), .B(in_18), .Cin(adder_18_carry), .Sum(out_69), .Carry(adder_17_carry));
  ADDER adder_18 (.A(in_43), .B(in_17), .Cin(adder_15_carry), .Sum(out_68), .Carry(adder_18_carry));
  ADDER adder_19 (.A(in_45), .B(in_19), .Cin(adder_17_carry), .Sum(out_70), .Carry(adder_19_carry));
  ADDER adder_20 (.A(in_46), .B(in_20), .Cin(adder_19_carry), .Sum(out_71), .Carry(adder_20_carry));
  ADDER adder_21 (.A(in_48), .B(in_22), .Cin(adder_22_carry), .Sum(out_73), .Carry(adder_21_carry));
  ADDER adder_22 (.A(in_47), .B(in_21), .Cin(adder_20_carry), .Sum(out_72), .Carry(adder_22_carry));
  ADDER adder_23 (.A(in_50), .B(in_24), .Cin(adder_24_carry), .Sum(out_75), .Carry(adder_23_carry));
  ADDER adder_24 (.A(in_49), .B(in_23), .Cin(adder_21_carry), .Sum(out_74), .Carry(adder_24_carry));
  ADDER adder_25 (.A(in_51), .B(in_25), .Cin(adder_23_carry), .Sum(out_76), .Carry(F_carry));
endmodule
