// Logisim project Temp.circ as structural Verilog: 1 circuit, main circuit main
module main (
  input  Reset,
  output CLK
);

  wire a1, a2, a3, b1, b2, b3, Bz, c1, c2, clock_1_out, d1, d2, f1, f2, i1, j_k_ff_1_q, j_k_ff_1_qn, LOAD_A,
       LOAD_B, LoadPc, or_1_out, R, s, S_qn, undriven, W;
  wire [3:0] IR_q, Mar, multiplexer_1_out, multiplexer_2_out, pcdata;
  wire [7:0] Ac_q, B, mdata, multiplexer_3_out, multiplexer_4_out, Res;

  Clock clock_1 (.out(clock_1_out));
  or or_1 (or_1_out, d1, d2);
  J_K_Flip_Flop j_k_ff_1 (
    .J(f1), .clk(clock_1_out), .K(f2), .Q(j_k_ff_1_q), .Qn(j_k_ff_1_qn));  // open: preset, en, reset
  Register #(.width(4), .trigger("falling")) IR (.D(B[7:4]), .en(i1), .Q(IR_q), .clk(clock_1_out), .clr(Reset));
  D_Flip_Flop u_S (.Qn(S_qn), .preset(s), .reset(Reset));  // open: clk, D, Q, en
  Multiplexer #(.width(4), .enable("false")) multiplexer_1 (.in0(Mar), .in1(B[3:0]), .out(multiplexer_1_out), .sel(c2));
  Counter #(.width(4), .max('hf)) PC (
    .load(LoadPc), .D(multiplexer_1_out), .count(c1), .Q(pcdata), .clk(CLK), .clr(Reset));  // open: carry
  Register #(.width(4)) u_MAR (.D(multiplexer_2_out), .en(or_1_out), .Q(Mar), .clk(CLK));  // open: clr
  Multiplexer #(.width(4), .enable("false")) multiplexer_2 (
    .in0(pcdata), .in1(B[3:0]), .out(multiplexer_2_out), .sel(d2));
  D_Flip_Flop E (.clk(CLK), .D(undriven));  // open: Q, Qn, preset, en, reset
  and and_1 (CLK, S_qn, clock_1_out);
  Multiplexer #(.select(2), .width(8), .enable("false")) multiplexer_3 (
    .in0({4'b0101, pcdata}), .in1(mdata), .in2(Ac_q), .out(multiplexer_3_out), .sel({b1, R}));  // open: in3
  Counter MBR (.load(LOAD_B), .D(multiplexer_3_out), .count(b2), .Q(B), .clk(CLK));  // open: carry, clr
  Register #(.trigger("falling")) Ac (.D(multiplexer_4_out), .en(LOAD_A), .Q(Ac_q), .clk(CLK));  // open: clr
  Multiplexer #(.width(8), .enable("false")) multiplexer_4 (.in0(Res), .in1(B), .out(multiplexer_4_out), .sel(a3));
  or or_2 (LOAD_A, a1, a2, a3);
  nor nor_1 (Bz, B[0], B[1], B[2], B[3], B[5], B[6], B[7], B[4]);
  or or_3 (LoadPc, c2, b3);
  or or_4 (LOAD_B, b1, R, b3);
  RAM #(.addrWidth(4), .bus("separate")) ram_1 (
    .addr(Mar), .din(B), .data(mdata), .str(W), .clk(CLK), .ld(R));  // open: sel, clr

  // Other names for the same wires on the sheet: BAD[3:0] = B[3:0]; Bop[3:0] = B[7:4]; sbit[1:0] = {b1, R}
endmodule
