// Logisim project Alu-prev.circ as structural Verilog: 10 circuits, main circuit 25 ALU
module _25_ALU (
  input  [1:0] Control,
  input  [24:0] A,
  input  [24:0] B,
  output [24:0] Output,
  output [3:0] Overflow_Carry_Zero_Negative
);

  wire zero_check_1_out;
  wire [24:0] and_1_a___b, n25_bit_adder_1_out_4, or_1_a___b;

  AND and_1 (.A(A), .B(B), .A___B(and_1_a___b));
  OR or_1 (.A(B), .B(A), .A___B(or_1_a___b));
  _25_bit_ADDER u_25_bit_adder_1 (
    .in_1(Control[0]), .A(A), .A_2(B), .out_4(n25_bit_adder_1_out_4),
    .Carry_Out(Overflow_Carry_Zero_Negative[2]), .Overflow(Overflow_Carry_Zero_Negative[3]));
  Multiplexer #(.select(2), .width(25), .enable("false")) multiplexer_1 (
    .in0(n25_bit_adder_1_out_4), .in1(n25_bit_adder_1_out_4), .in2(and_1_a___b), .in3(or_1_a___b),
    .out(Output), .sel(Control));
  Negative_check negative_check_1 (.Input(Output), .Out(Overflow_Carry_Zero_Negative[0]));
  not not_1 (Overflow_Carry_Zero_Negative[1], zero_check_1_out);
  Zero_Check zero_check_1 (.Input(Output), .Out(zero_check_1_out));

  // Notes on the sheet:
  //   2207106
  //   00- Adder
  //   01-Substactor
  //   10-And
  //   11-Or
endmodule

module AND (
  input  [24:0] A,
  input  [24:0] B,
  output [24:0] A___B
);

  assign A___B = A & B;  // AND_Gate _25_bit_AND, 25 bits wide

  // Notes on the sheet:
  //   2207106
endmodule

module OR (
  input  [24:0] A,
  input  [24:0] B,
  output [24:0] A___B
);

  assign A___B = A | B;  // OR_Gate _25_bit_OR, 25 bits wide
endmodule

module _1_bit_ADDER (
  input  Cin,
  input  A,
  input  B,
  output out_4
);

  wire xor_1_out;

  xor xor_1 (xor_1_out, A, B);
  xor SUM (out_4, Cin, xor_1_out);

  // Notes on the sheet:
  //   2207106
endmodule

// ADDER
module _25_bit_ADDER (
  input  in_1,
  input  [24:0] A,
  input  [24:0] A_2,
  output [24:0] out_4,
  output Carry_Out,
  output Overflow
);

  wire _1, _2, _3, _4, _5, _6, _7, _8, _9, _10, _11, _12, _13, _14, _15, _16, _17, _18, _19, _20, _21, _22,
       _23, _24, aa, and_1_out, and_2_out, bb, cc, dd, ee, ff, gg, hh, ii, jj, kk, ll, mm, nn, not_1_out,
       not_2_out, not_3_out, oo, pp, qq, rr, ss, tt, uu, vv, ww, xx, yy;
  wire [24:0] bit_extender_1_out;

  assign bit_extender_1_out = {{24{in_1}}, in_1};  // Bit_Extender bit_extender_1
  _25_bit_CLG u_25_bit_clg_1 (
    .Cin(in_1), .A(A), .B(A_2),
    .Cout({Carry_Out, _24, _23, _22, _21, _20, _19, _18, _17, _16, _15, _14, _13, _12, _11, _10, _9, _8, _7, _6, _5, _4, _3, _2, _1}));
  assign {yy, xx, ww, vv, uu, tt, ss, rr, qq, pp, oo, nn, mm, ll, kk, jj, ii, hh, gg, ff, ee, dd, cc, bb, aa} = bit_extender_1_out ^ A_2;  // XOR_Gate xor_1, 25 bits wide
  _1_bit_ADDER u_1_bit_adder_1 (.Cin(in_1), .A(A[0]), .B(aa), .out_4(out_4[0]));
  _1_bit_ADDER u_1_bit_adder_2 (.Cin(_1), .A(A[1]), .B(bb), .out_4(out_4[1]));
  _1_bit_ADDER u_1_bit_adder_3 (.Cin(_2), .A(A[2]), .B(cc), .out_4(out_4[2]));
  _1_bit_ADDER u_1_bit_adder_4 (.Cin(_3), .A(A[3]), .B(dd), .out_4(out_4[3]));
  _1_bit_ADDER u_1_bit_adder_5 (.Cin(_4), .A(A[4]), .B(ee), .out_4(out_4[4]));
  _1_bit_ADDER u_1_bit_adder_6 (.Cin(_5), .A(A[5]), .B(ff), .out_4(out_4[5]));
  _1_bit_ADDER u_1_bit_adder_7 (.Cin(_6), .A(A[6]), .B(gg), .out_4(out_4[6]));
  _1_bit_ADDER u_1_bit_adder_8 (.Cin(_7), .A(A[7]), .B(hh), .out_4(out_4[7]));
  _1_bit_ADDER u_1_bit_adder_9 (.Cin(_8), .A(A[8]), .B(ii), .out_4(out_4[8]));
  _1_bit_ADDER u_1_bit_adder_10 (.Cin(_9), .A(A[9]), .B(jj), .out_4(out_4[9]));
  _1_bit_ADDER u_1_bit_adder_11 (.Cin(_10), .A(A[10]), .B(kk), .out_4(out_4[10]));
  _1_bit_ADDER u_1_bit_adder_12 (.Cin(_11), .A(A[11]), .B(ll), .out_4(out_4[11]));
  _1_bit_ADDER u_1_bit_adder_13 (.Cin(_12), .A(A[12]), .B(mm), .out_4(out_4[12]));
  _1_bit_ADDER u_1_bit_adder_14 (.Cin(_13), .A(A[13]), .B(nn), .out_4(out_4[13]));
  _1_bit_ADDER u_1_bit_adder_15 (.Cin(_14), .A(A[14]), .B(oo), .out_4(out_4[14]));
  _1_bit_ADDER u_1_bit_adder_16 (.Cin(_15), .A(A[15]), .B(pp), .out_4(out_4[15]));
  _1_bit_ADDER u_1_bit_adder_17 (.Cin(_16), .A(A[16]), .B(qq), .out_4(out_4[16]));
  _1_bit_ADDER u_1_bit_adder_18 (.Cin(_17), .A(A[17]), .B(rr), .out_4(out_4[17]));
  _1_bit_ADDER u_1_bit_adder_19 (.Cin(_18), .A(A[18]), .B(ss), .out_4(out_4[18]));
  _1_bit_ADDER u_1_bit_adder_20 (.Cin(_19), .A(A[19]), .B(tt), .out_4(out_4[19]));
  _1_bit_ADDER u_1_bit_adder_21 (.Cin(_20), .A(A[20]), .B(uu), .out_4(out_4[20]));
  _1_bit_ADDER u_1_bit_adder_22 (.Cin(_21), .A(A[21]), .B(vv), .out_4(out_4[21]));
  _1_bit_ADDER u_1_bit_adder_23 (.Cin(_22), .A(A[22]), .B(ww), .out_4(out_4[22]));
  _1_bit_ADDER u_1_bit_adder_24 (.Cin(_23), .A(A[23]), .B(xx), .out_4(out_4[23]));
  _1_bit_ADDER u_1_bit_adder_25 (.Cin(_24), .A(A[24]), .B(yy), .out_4(out_4[24]));
  not not_1 (not_1_out, out_4[24]);
  not not_2 (not_2_out, A[24]);
  not not_3 (not_3_out, yy);
  and and_1 (and_1_out, not_1_out, A[24], yy);
  and and_2 (and_2_out, out_4[24], not_2_out, not_3_out);
  or or_1 (Overflow, and_1_out, and_2_out);

  // Other names for the same wires on the sheet: _25 = Carry_Out; a_t = A[0]; b = A[1]; c = A[2]; d = A[3]; e = A[4];
  //   f = A[5]; g = A[6]; h = A[7]; i = A[8]; j = A[9]; k = A[10]; l = A[11]; m = A[12]; n = A[13]; o = A[14];
  //   p = A[15]; q = A[16]; r = A[17]; s = A[18]; t = A[19]; u = A[20]; v = A[21]; w = A[22]; x = A[23]; y = A[24];
  //   Cin = in_1
endmodule

module _4_bit_CLG (
  input  Cin,
  input  [3:0] A,
  input  [3:0] B,
  output C1,
  output C2,
  output C3,
  output C4
);

  wire and_5_out, and_6_out, and_7_out, and_8_out, and_9_out, and_10_out, and_11_out, and_12_out, and_13_out,
       and_14_out, G0, G1, G2, G3, xor_1_out, xor_2_out, xor_3_out, xor_4_out, xor_5_out, xor_6_out,
       xor_7_out, xor_8_out;

  xor xor_1 (xor_1_out, Cin, B[0]);
  xor xor_2 (xor_2_out, Cin, B[1]);
  xor xor_3 (xor_3_out, Cin, B[2]);
  xor xor_4 (xor_4_out, Cin, B[3]);
  xor xor_5 (xor_5_out, A[0], xor_1_out);
  xor xor_6 (xor_6_out, A[1], xor_2_out);
  xor xor_7 (xor_7_out, A[2], xor_3_out);
  xor xor_8 (xor_8_out, A[3], xor_4_out);
  and and_1 (G0, A[0], xor_1_out);
  and and_2 (G1, A[1], xor_2_out);
  and and_3 (G2, A[2], xor_3_out);
  and and_4 (G3, A[3], xor_4_out);
  and and_5 (and_5_out, Cin, xor_5_out);
  and and_6 (and_6_out, G0, xor_6_out);
  and and_7 (and_7_out, Cin, xor_5_out, xor_6_out);
  and and_8 (and_8_out, xor_7_out, G1);
  and and_9 (and_9_out, xor_6_out, xor_7_out, G0);
  and and_10 (and_10_out, xor_5_out, xor_6_out, xor_7_out, Cin);
  and and_11 (and_11_out, xor_8_out, G2);
  and and_12 (and_12_out, xor_8_out, xor_7_out, G1);
  and and_13 (and_13_out, xor_6_out, xor_7_out, xor_8_out, G0);
  and and_14 (and_14_out, xor_5_out, xor_6_out, xor_7_out, xor_8_out, Cin);
  or or_1 (C1, G0, and_5_out);
  or or_2 (C2, G1, and_6_out, and_7_out);
  or or_3 (C3, G2, and_8_out, and_9_out, and_10_out);
  or or_4 (C4, G3, and_11_out, and_12_out, and_13_out, and_14_out);
endmodule

module _1_BIT_CLG (
  input  Cin,
  input  A,
  input  B,
  output Cout
);

  wire and_1_out, and_2_out, xor_1_out, xor_2_out;

  xor xor_1 (xor_1_out, Cin, B);
  xor xor_2 (xor_2_out, A, xor_1_out);
  and and_1 (and_1_out, xor_1_out, A);
  and and_2 (and_2_out, xor_2_out, A);
  or or_1 (Cout, and_1_out, and_2_out);
endmodule

module _25_bit_CLG (
  input  Cin,
  input  [24:0] A,
  input  [24:0] B,
  output [24:0] Cout
);

  _4_bit_CLG u_4_bit_clg_1 (.Cin(Cin), .A(A[3:0]), .B(B[3:0]), .C1(Cout[0]), .C2(Cout[1]), .C3(Cout[2]), .C4(Cout[3]));
  _4_bit_CLG u_4_bit_clg_2 (
    .Cin(Cout[3]), .A(A[7:4]), .B(B[7:4]), .C1(Cout[4]), .C2(Cout[5]), .C3(Cout[6]), .C4(Cout[7]));
  _4_bit_CLG u_4_bit_clg_3 (
    .Cin(Cout[7]), .A(A[11:8]), .B(B[11:8]), .C1(Cout[8]), .C2(Cout[9]), .C3(Cout[10]), .C4(Cout[11]));
  _4_bit_CLG u_4_bit_clg_4 (
    .Cin(Cout[11]), .A(A[15:12]), .B(B[15:12]), .C1(Cout[12]), .C2(Cout[13]), .C3(Cout[14]), .C4(Cout[15]));
  _4_bit_CLG u_4_bit_clg_5 (
    .Cin(Cout[15]), .A(A[19:16]), .B(B[19:16]), .C1(Cout[16]), .C2(Cout[17]), .C3(Cout[18]), .C4(Cout[19]));
  _4_bit_CLG u_4_bit_clg_6 (
    .Cin(Cout[19]), .A(A[23:20]), .B(B[23:20]), .C1(Cout[20]), .C2(Cout[21]), .C3(Cout[22]), .C4(Cout[23]));
  _1_BIT_CLG u_1_bit_clg_1 (.Cin(Cout[23]), .A(A[24]), .B(B[24]), .Cout(Cout[24]));
endmodule

// Neg
module Negative_check (
  input  [24:0] Input,
  output Out
);


  assign Out = Input[24];
endmodule

// Zero
module Zero_Check (
  input  [24:0] Input,
  output Out
);

  or or_1 (Out, Input[0], Input[1], Input[2], Input[3], Input[4], Input[5], Input[6], Input[7], Input[8], Input[9], Input[10], Input[11], Input[12], Input[13], Input[14], Input[15], Input[16], Input[17], Input[18], Input[19], Input[20], Input[21], Input[22], Input[23], Input[24]);
endmodule
