// Logisim project ASSIGN.circ as structural Verilog: 2 circuits, main circuit main
module main (
  input  c_1,
  input  A3,
  input  A2,
  input  A1,
  input  A0,
  input  B3,
  input  B2,
  input  B1,
  input  B0,
  output C3,
  output S0,
  output S1,
  output S2,
  output S3
);

  wire and_1_out, and_2_out, and_3_out, and_4_out, and_5_out, and_6_out, and_7_out, and_8_out, and_9_out,
       and_10_out, C0_out, C1_out, C2_out, G0_out, G1_out, G2_out, G3_out, P0_out, P1_out, P2_out, P3_out;

  and G0 (G0_out, A0, B0);
  and G1 (G1_out, A1, B1);
  and G2 (G2_out, A2, B2);
  and G3 (G3_out, A3, B3);
  xor P0 (P0_out, A0, B0);
  xor P1 (P1_out, A1, B1);
  xor P2 (P2_out, A2, B2);
  xor P3 (P3_out, A3, B3);
  ExactlyOne u_S0 (.out(S0), .in0(c_1), .in1(A0), .in2(B0));
  or C0 (C0_out, G0_out, and_1_out);
  and and_1 (and_1_out, c_1, P0_out);
  ExactlyOne u_S1 (.out(S1), .in0(B1), .in1(A1), .in2(C0_out));
  and and_2 (and_2_out, G0_out, P1_out);
  and and_3 (and_3_out, c_1, P0_out, P1_out);
  and and_4 (and_4_out, P0_out, P1_out, P2_out, c_1);
  and and_5 (and_5_out, P2_out, P1_out, G0_out);
  and and_6 (and_6_out, P2_out, G1_out);
  or C1 (C1_out, G1_out, and_2_out, and_3_out);
  and and_7 (and_7_out, c_1, P0_out, P1_out, P2_out, P3_out);
  and and_8 (and_8_out, P3_out, P1_out, P2_out, G0_out);
  and and_9 (and_9_out, P3_out, P2_out, G1_out);
  and and_10 (and_10_out, G2_out, P3_out);
  ExactlyOne u_S2 (.out(S2), .in0(B2), .in1(A2), .in2(C1_out));
  or C2 (C2_out, G2_out, and_4_out, and_5_out, and_6_out);
  or u_c3 (C3, and_7_out, and_8_out, and_9_out, and_10_out, G3_out);
  ExactlyOne u_S3 (.out(S3), .in0(B3), .in1(A3), .in2(C2_out));

  // Notes on the sheet:
  //   2207055
endmodule

module _4_BIT_MULTIPLIER (
  input  x3,
  input  X2,
  input  X1,
  input  X0,
  input  Y0,
  input  Y2,
  input  Y2_2,
  input  Y1,
  input  C_1,
  input  in_10,
  output P0,
  output P1,
  output P2,
  output P3,
  output P4,
  output P5,
  output P6,
  output P7
);

  wire main_1_p8, main_1_p10, main_1_p12, main_1_p14, main_2_p5, main_2_p7, main_2_p9, main_2_p11,
       main_2_p14, X0Y1_out, X0Y2_2_out, X0Y2_out, X1Y1_out, X1Y2_2_out, X1Y2_out, X2Y0_out, X2Y1_out,
       X2Y2_2_out, X2Y2_out, X3Y0_out, X3Y1_out, X3Y2_2_out, X3Y2_out;

  and X2Y1 (X2Y1_out, Y1, X2);
  and X3Y1 (X3Y1_out, Y1, x3);
  and X3Y2 (X3Y2_out, Y2_2, x3);
  and X2Y2 (X2Y2_out, Y2_2, X2);
  and X2Y2_2 (X2Y2_2_out, Y2, X2);
  and X3Y2_2 (X3Y2_2_out, Y2, x3);
  and X1Y1 (X1Y1_out, Y1, X1);
  and X1Y2 (X1Y2_out, Y2_2, X1);
  and X1Y2_2 (X1Y2_2_out, Y2, X1);
  and X0Y1 (X0Y1_out, Y1, X0);
  and X0Y2 (X0Y2_out, Y2_2, X0);
  and X0Y2_2 (X0Y2_2_out, Y2, X0);
  // main main_1: pin names not known; wires that end beside it: X3Y2_2_out, C_1, X2Y2_2_out, X1Y2_2_out, P7, X0Y2_2_out, P6, main_1_p8, P5, main_1_p10, P4, main_1_p12, P3, main_1_p14
  and X3Y0 (X3Y0_out, Y0, x3);
  and X2Y0 (X2Y0_out, Y0, X2);
  // main main_2: pin names not known; wires that end beside it: X3Y1_out, C_1, X2Y1_out, X1Y1_out, main_2_p5, X0Y1_out, main_2_p7, in_10, main_2_p9, X3Y0_out, main_2_p11, X2Y0_out, P1, main_2_p14
  // main main_3: pin names not known; wires that end beside it: X3Y2_out, C_1, X2Y2_out, X1Y2_out, main_1_p8, X0Y2_out, main_1_p10, main_2_p5, main_1_p12, main_2_p7, main_1_p14, main_2_p9, P2, main_2_p11
  and X1Y0 (main_2_p14, Y0, X1);
  and X0Y0 (P0, Y0, X0);

  // Notes on the sheet:
  //   2207106
endmodule
