// Logisim project CLG temp.circ as structural Verilog: 1 circuit, main circuit main
module main (
  input  C_1,
  input  A0,
  input  B0,
  input  A1,
  input  B1,
  input  A2,
  input  B2,
  input  A3,
  input  B3,
  output out_10,
  output out_11,
  output out_12,
  output out_13,
  output out_14
);

  wire C0_out, C1_out, C2_out, G0_out, G0P1P2_out, G0P1P2P3_out, G1_out, G1P2_out, G1P2P3_out, G2_out,
       G2P3_out, G3_out, P0_out, P0C_1_out, P0C_1P1_out, P0P1P2C_1_out, P0P1P2P3C_1_out, P1_out, P1G0_out,
       P2_out, P3_out;

  and G0 (G0_out, A0, B0);
  or C0 (C0_out, G0_out, P0C_1_out);
  ExactlyOne S0 (.out(out_11), .in0(C_1), .in1(A0), .in2(B0));
  xor P0 (P0_out, A0, B0);
  and P0C_1 (P0C_1_out, C_1, P0_out);
  and G1 (G1_out, A1, B1);
  and P1G0 (P1G0_out, G0_out, P1_out);
  xor P1 (P1_out, A1, B1);
  and P0C_1P1 (P0C_1P1_out, P0C_1_out, P1_out);
  or C1 (C1_out, G1_out, P1G0_out, P0C_1P1_out);
  ExactlyOne S1 (.out(out_12), .in0(C0_out), .in1(A1), .in2(B1));
  and G1P2 (G1P2_out, G1_out, P2_out);
  and G2 (G2_out, A2, B2);
  and G0P1P2 (G0P1P2_out, P1G0_out, P2_out);
  or C2 (C2_out, G1P2_out, G0P1P2_out, G2_out, P0P1P2C_1_out);
  ExactlyOne S2 (.out(out_13), .in0(A2), .in1(C1_out), .in2(B2));
  xor P2 (P2_out, A2, B2);
  and P0P1P2C_1 (P0P1P2C_1_out, P0C_1P1_out, P2_out);
  and G3 (G3_out, A3, B3);
  ExactlyOne S3 (.out(out_14), .in0(C2_out), .in1(A3), .in2(B3));
  xor P3 (P3_out, A3, B3);
  and G2P3 (G2P3_out, G2_out, P3_out);
  and G0P1P2P3 (G0P1P2P3_out, G0P1P2_out, P3_out);
  and G1P2P3 (G1P2P3_out, G1P2_out, P3_out);
  or C3 (out_10, G3_out, G2P3_out, G1P2P3_out, G0P1P2P3_out, P0P1P2P3C_1_out);
  and P0P1P2P3C_1 (P0P1P2P3C_1_out, P0P1P2C_1_out, P3_out);
endmodule
