// Logisim project nor trial - Copy.circ as structural Verilog: 2 circuits, main circuit main
module main (
  input  G2,
  input  G1,
  input  G0
);

  wire nor_1_out_3, nor_2_out_3, nor_3_out_3, nor_4_out_3, nor_5_out_3, nor_6_out_3, nor_7_out_3,
       nor_8_out_3, nor_9_out_3, nor_10_out_3, nor_11_out_3, nor_12_out_3;

  \nor  nor_1 (.in_1(G2), .in_2(G2), .out_3(nor_1_out_3));
  \nor  nor_2 (.in_1(G1), .in_2(G1), .out_3(nor_2_out_3));
  \nor  nor_3 (.in_1(nor_11_out_3), .in_2(nor_11_out_3), .out_3(nor_3_out_3));
  \nor  nor_4 (.in_1(G0), .in_2(G0), .out_3(nor_4_out_3));
  \nor  nor_5 (.in_1(G2), .in_2(nor_2_out_3), .out_3(nor_5_out_3));
  \nor  nor_6 (.in_1(nor_1_out_3), .in_2(G1), .out_3(nor_6_out_3));
  \nor  nor_7 (.in_1(nor_11_out_3), .in_2(nor_4_out_3), .out_3(nor_7_out_3));
  \nor  nor_8 (.in_1(nor_3_out_3), .in_2(G0), .out_3(nor_8_out_3));
  \nor  nor_9 (.in_1(nor_5_out_3), .in_2(nor_6_out_3), .out_3(nor_9_out_3));
  \nor  nor_10 (.in_1(nor_7_out_3), .in_2(nor_8_out_3), .out_3(nor_10_out_3));
  \nor  nor_11 (.in_1(nor_9_out_3), .in_2(nor_9_out_3), .out_3(nor_11_out_3));
  \nor  nor_12 (.in_1(nor_10_out_3), .in_2(nor_10_out_3), .out_3(nor_12_out_3));
  LED B1 (.in(nor_11_out_3));
  LED B2 (.in(G2));
  LED B0 (.in(nor_12_out_3));

  // Notes on the sheet:
  //   A'
  //   B'
  //   A'
  //   B'
endmodule

// NOR
module \nor  (
  input  in_1,
  input  in_2,
  output out_3
);

  wire or_1_out;

  or or_1 (or_1_out, in_1, in_2);
  not not_1 (out_3, or_1_out);
endmodule
