// Logisim project dld LAB TASK.circ as structural Verilog: 2 circuits, main circuit main
module main (
  output out_1,
  output out_2,
  output out_3
);

  wire and_1_out, and_2_out, and_3_out, and_4_out, and_5_out, clock_1_out, or_1_out, or_2_out, or_3_out,
       Q0_qn, Q1_qn, Q2_qn, Q3_q, Q3_qn;

  T_Flip_Flop t_ff_1 ();  // open: clk, T, Q, Qn, preset, reset, en
  Clock clock_1 (.out(clock_1_out));
  and and_1 (and_1_out, Q1_qn, Q3_qn);
  and and_2 (and_2_out, Q0_qn, Q1_qn);
  T_Flip_Flop Q0 (.clk(clock_1_out), .T(and_1_out), .Q(out_3), .Qn(Q0_qn));  // open: preset, reset, en
  and and_3 (and_3_out, out_3, out_2);
  or or_1 (or_1_out, and_2_out, and_3_out, Q3_q);
  T_Flip_Flop Q1 (.clk(clock_1_out), .T(or_1_out), .Q(out_2), .Qn(Q1_qn));  // open: preset, reset, en
  or or_2 (or_2_out, and_2_out, out_1);
  T_Flip_Flop Q2 (.clk(clock_1_out), .T(or_2_out), .Q(out_1), .Qn(Q2_qn));  // open: preset, reset, en
  and and_4 (and_4_out, out_2, Q2_qn);
  and and_5 (and_5_out, out_3, Q2_qn);
  T_Flip_Flop Q3 (.clk(clock_1_out), .T(or_3_out), .Q(Q3_q), .Qn(Q3_qn));  // open: preset, reset, en
  or or_3 (or_3_out, and_4_out, and_5_out, Q3_q);
endmodule

module _7_segment (
  input  A
);

  wire a_out, A_prime_out, and_1_out, and_2_out, and_3_out, b_out, B_prime_C_out, B_prime_D_prime_out,
       B_prime_out, BC_prime_out, BD_out, c_out, C_prime_D_prime_out, C_prime_out, CD_prime_out, d_out,
       D_prime_out, e_out, f_out, g_out, main_1_out_1, main_1_out_2, main_1_out_3;

  main main_1 (.out_1(main_1_out_1), .out_2(main_1_out_2), .out_3(main_1_out_3));
  not A_prime (A_prime_out, A);
  not B_prime (B_prime_out, main_1_out_1);
  not C_prime (C_prime_out, main_1_out_2);
  not D_prime (D_prime_out, main_1_out_3);
  and BD (BD_out, main_1_out_1, main_1_out_3);
  and B_prime_D_prime (B_prime_D_prime_out, B_prime_out, D_prime_out);
  and C_prime_D_prime (C_prime_D_prime_out, C_prime_out, D_prime_out);
  and and_1 (and_1_out, main_1_out_2, main_1_out_3);
  and CD_prime (CD_prime_out, main_1_out_2, D_prime_out);
  and and_2 (and_2_out, main_1_out_1, C_prime_out, main_1_out_3);
  and B_prime_C (B_prime_C_out, B_prime_out, main_1_out_2);
  and BC_prime (BC_prime_out, main_1_out_1, C_prime_out);
  and and_3 (and_3_out, main_1_out_1, D_prime_out);
  or u_a (a_out, A, main_1_out_2, BD_out, B_prime_D_prime_out);
  or b (b_out, B_prime_out, C_prime_D_prime_out, and_1_out);
  or c (c_out, main_1_out_1, C_prime_out, main_1_out_3);
  or d (d_out, B_prime_D_prime_out, A, CD_prime_out, and_2_out, B_prime_C_out);
  or e (e_out, B_prime_D_prime_out, CD_prime_out);
  or f (f_out, A, BC_prime_out, and_3_out, C_prime_D_prime_out);
  or g (g_out, A, B_prime_C_out, CD_prime_out, BC_prime_out);
  _7_Segment_Display u_7_segment_display_1 (
    .g(g_out), .f(f_out), .a(a_out), .b(b_out), .e(e_out), .d(d_out), .c(c_out));  // open: dp
endmodule
