// Logisim project dld assignment lab 2.circ as structural Verilog: 1 circuit, main circuit main
module main (
  output out_1,
  output out_2,
  output out_3
);

  wire and_1_out, and_2_out, and_3_out, and_4_out, and_5_out, clock_1_out, or_1_out, or_2_out, or_3_out,
       Q0_qn, Q1_qn, Q2_qn, Q3_q, Q3_qn;

  T_Flip_Flop t_ff_1 ();  // open: clk, T, Q, Qn, preset, reset, en
  Clock clock_1 (.out(clock_1_out));
  and and_1 (and_1_out, Q1_qn, Q3_qn);
  and and_2 (and_2_out, Q0_qn, Q1_qn);
  T_Flip_Flop Q0 (.clk(clock_1_out), .T(and_1_out), .Q(out_3), .Qn(Q0_qn));  // open: preset, reset, en
  and and_3 (and_3_out, out_3, out_2);
  or or_1 (or_1_out, and_2_out, and_3_out, Q3_q);
  T_Flip_Flop Q1 (.clk(clock_1_out), .T(or_1_out), .Q(out_2), .Qn(Q1_qn));  // open: preset, reset, en
  or or_2 (or_2_out, and_2_out, out_1);
  T_Flip_Flop Q2 (.clk(clock_1_out), .T(or_2_out), .Q(out_1), .Qn(Q2_qn));  // open: preset, reset, en
  and and_4 (and_4_out, out_2, Q2_qn);
  and and_5 (and_5_out, out_3, Q2_qn);
  T_Flip_Flop Q3 (.clk(clock_1_out), .T(or_3_out), .Q(Q3_q), .Qn(Q3_qn));  // open: preset, reset, en
  or or_3 (or_3_out, and_4_out, and_5_out, Q3_q);
endmodule
