// Logisim project 2207106.circ as structural Verilog: 2 circuits, main circuit main
module main (
  input  F2,
  input  F1,
  input  F0,
  input  in_4
);

  wire _7_SEG_out_5, _7_SEG_out_6, _7_SEG_out_7, _7_SEG_out_8, _7_SEG_out_9, _7_SEG_out_10, _7_SEG_out_11,
       and_1_out, and_2_out, and_3_out, and_4_out, and_5_out, and_6_out, and_7_out, and_8_out, and_9_out,
       and_10_out, and_11_out, and_12_out, and_13_out, and_14_out, clock_1_out, d_ff_1_q, d_ff_1_qn,
       d_ff_2_q, d_ff_2_qn, d_ff_3_q, d_ff_3_qn, not_1_out, not_2_out, not_3_out, or_1_out, or_2_out,
       Q0_t_out, Q1_t_out, Q2_t_out;

  not not_1 (not_1_out, F2);
  not not_2 (not_2_out, F1);
  not not_3 (not_3_out, F0);
  and and_1 (and_1_out, d_ff_2_q, d_ff_3_q, F2);
  and and_2 (and_2_out, F2, d_ff_1_q);
  and and_3 (and_3_out, d_ff_3_q, F1);
  and and_4 (and_4_out, F1, d_ff_2_q);
  and and_5 (and_5_out, d_ff_3_q, d_ff_2_qn, F2);
  and and_6 (and_6_out, F2, d_ff_2_q, d_ff_3_qn);
  and and_7 (and_7_out, d_ff_3_q, d_ff_2_q, not_1_out);
  and and_8 (and_8_out, not_1_out, d_ff_1_q);
  and and_9 (and_9_out, d_ff_3_qn, d_ff_2_qn, F1);
  and and_10 (and_10_out, F1, d_ff_2_q, F0);
  and and_11 (and_11_out, d_ff_2_qn, F0, not_2_out);
  and and_12 (and_12_out, not_2_out, d_ff_3_qn, d_ff_2_q);
  and and_13 (and_13_out, d_ff_1_qn, d_ff_3_qn, F2);
  and and_14 (and_14_out, d_ff_1_q, not_1_out);
  or Q2_t (Q2_t_out, and_1_out, and_2_out);
  or or_1 (or_1_out, and_3_out, and_4_out);
  or Q1_t (Q1_t_out, or_1_out, and_5_out, and_6_out, and_7_out, and_8_out);
  or or_2 (or_2_out, and_9_out, and_10_out);
  or Q0_t (Q0_t_out, or_2_out, and_11_out, and_12_out, and_13_out, and_14_out);
  D_Flip_Flop d_ff_1 (.clk(clock_1_out), .D(Q2_t_out), .Q(d_ff_1_q), .Qn(d_ff_1_qn));  // open: preset, en, reset
  D_Flip_Flop d_ff_2 (.clk(clock_1_out), .D(Q1_t_out), .Q(d_ff_2_q), .Qn(d_ff_2_qn));  // open: preset, en, reset
  D_Flip_Flop d_ff_3 (.clk(clock_1_out), .D(Q0_t_out), .Q(d_ff_3_q), .Qn(d_ff_3_qn));  // open: preset, en, reset
  Clock clock_1 (.out(clock_1_out));
  _7_SEGMENT _7_SEG (
    .in_1(d_ff_3_q), .in_2(d_ff_2_q), .in_3(d_ff_1_q), .A(in_4), .out_5(_7_SEG_out_5), .out_6(_7_SEG_out_6),
    .out_7(_7_SEG_out_7), .out_8(_7_SEG_out_8), .out_9(_7_SEG_out_9), .out_10(_7_SEG_out_10),
    .out_11(_7_SEG_out_11));
  _7_Segment_Display u_7_segment_display_1 (
    .g(_7_SEG_out_11), .f(_7_SEG_out_10), .a(_7_SEG_out_5), .b(_7_SEG_out_6), .e(_7_SEG_out_9),
    .d(_7_SEG_out_8), .c(_7_SEG_out_7));  // open: dp

  // Notes on the sheet:
  //   2207106
  //   Q2
  //   Q1
  //   Q2'
  //   Q1'
  //   Q0
  //   Q0'
endmodule

module _7_SEGMENT (
  input  in_1,
  input  in_2,
  input  in_3,
  input  A,
  output out_5,
  output out_6,
  output out_7,
  output out_8,
  output out_9,
  output out_10,
  output out_11
);

  wire A_prime_out, and_1_out, and_2_out, and_3_out, B_prime_C_out, B_prime_D_prime_out, B_prime_out,
       BC_prime_out, BD_out, C_prime_D_prime_out, C_prime_out, CD_prime_out, D_prime_out, undriven,
       undriven_2, undriven_3, undriven_4, undriven_5, undriven_6, undriven_7;

  not A_prime (A_prime_out, A);
  not B_prime (B_prime_out, in_3);
  not C_prime (C_prime_out, in_2);
  not D_prime (D_prime_out, in_1);
  and BD (BD_out, in_3, in_1);
  and B_prime_D_prime (B_prime_D_prime_out, B_prime_out, D_prime_out);
  and C_prime_D_prime (C_prime_D_prime_out, C_prime_out, D_prime_out);
  and and_1 (and_1_out, in_2, in_1);
  and CD_prime (CD_prime_out, in_2, D_prime_out);
  and and_2 (and_2_out, in_3, C_prime_out, in_1);
  and B_prime_C (B_prime_C_out, B_prime_out, in_2);
  and BC_prime (BC_prime_out, in_3, C_prime_out);
  and and_3 (and_3_out, in_3, D_prime_out);
  or u_a (out_5, A, in_2, BD_out, B_prime_D_prime_out);
  or b (out_6, B_prime_out, C_prime_D_prime_out, and_1_out);
  or c (out_7, in_3, C_prime_out, in_1);
  or d (out_8, B_prime_D_prime_out, A, CD_prime_out, and_2_out, B_prime_C_out);
  or e (out_9, B_prime_D_prime_out, CD_prime_out);
  or f (out_10, A, BC_prime_out, and_3_out, C_prime_D_prime_out);
  or g (out_11, A, B_prime_C_out, CD_prime_out, BC_prime_out);
  _7_Segment_Display u_7_segment_display_1 (
    .g(undriven_5), .f(undriven_6), .a(undriven), .b(undriven_2), .e(undriven_7), .d(undriven_4),
    .c(undriven_3));  // open: dp

  // Notes on the sheet:
  //   2207106
endmodule
